# Fritzing sketch Door Pi (saved by Fritzing 0.9.4)
circuit board: 8.8cm x 5.9cm
breadboards: 1

parts:
  U3 = AQT212GH [package="DIP (Dual Inline) [THT]"]
  U2 = AQT212GH [package="DIP (Dual Inline) [THT]"]
  LED2 = l710a8ge dual led [package=THT]
  LLC1 = Logic Level Converter [package="Breakout board"]
  U1 = TSR2 Series
  12V = 2.1mm DC Barrel Jack
  Fuse2 = Fuse with Handler [part_number=Htc-15m]
  R3 = Resistor [tolerance=±5% resistance=470 package=THT]
  PWR = LED - 5mm [color="Red (633nm)" package="5 mm [THT]"]
  R4 = Resistor [tolerance=±5% resistance=470 package=THT]
  R2 = Resistor [tolerance=±5% resistance=470 package=THT]
  R6 = Resistor [tolerance=±5% resistance=10k package=THT]
  C1 = Ceramic Capacitor [capacitance=0.1µF package="100 mil [THT, multilayer]"]
  R5 = Resistor [tolerance=±5% resistance=100k package=THT]
  R1 = Resistor [tolerance=±5% resistance=470 package=THT]
  U4 = AQT212GH [package="DIP (Dual Inline) [THT]"]
  Pi_Connector = Raspberry Pi Header 40pin [package=THT]
  Door_Reader = Camdenboss CTB0158-8 [package=THT]
  LED1 = l710a8ge dual led [package=THT]
  Bell_12V = Camdenboss CTB0158-2 [package=THT]
  Strike = Camdenboss CTB0158-2 [package=THT]
  Bell_CC = Camdenboss CTB0158-2 [package=THT]
  3_3V = Camdenboss CTB0158-2 [package=THT]
  Sensor = Camdenboss CTB0158-2 [package=THT]

nets:
  N1: U3.pin1, Pi_Connector.IO4
  GND: U3.pin2, U2.pin2, LED2.pin2, LED2.pin4, LLC1.L-GND, LLC1.H-GND, U1.GND, 12V.GND, 12V.sleeve, PWR.cathode, C1.1, U4.pin2, Pi_Connector.GND, Door_Reader.pin2, Door_Reader.pin8, LED1.pin2, LED1.pin4, Bell_12V.pin1, Strike.pin1, 3_3V.pin2, Sensor.pin1
  N2: U3.pin3, U2.pin3, 12V.center_(V+), Fuse2.Connector2, PWR.anode, Door_Reader.pin1
  N3: U3.pin4, R3.Pin_1, Bell_12V.pin2
  N4: U2.pin1, Pi_Connector.IO17
  N5: U2.pin4, R4.Pin_1, Strike.pin2
  N6: LED2.pin1, R3.Pin_0
  N7: LED2.pin3, R4.Pin_0
  N8: LLC1.LV1, Pi_Connector.IO14
  N9: LLC1.LV2, Pi_Connector.IO15
  N10: LLC1.LV, R5.Pin_0, Pi_Connector.3V3, 3_3V.pin1
  N11: LLC1.LV3, Pi_Connector.IO22#12
  N12: LLC1.LV4, Pi_Connector.IO22#14
  N13: LLC1.HV4, Door_Reader.pin6
  N14: LLC1.HV3, Door_Reader.pin5
  N15: LLC1.HV, U1.OUT, Pi_Connector.5V
  N16: LLC1.HV2, Door_Reader.pin4
  N17: LLC1.HV1, Door_Reader.pin3
  N18: U1.IN, Fuse2.Connector1
  N19: R2.Pin_0, LED1.pin3
  N20: R2.Pin_1, Pi_Connector.IO19
  N21: R6.Pin_0, C1.0, Pi_Connector.IO5
  N22: R6.Pin_1, R5.Pin_1, Door_Reader.pin7
  N23: R1.Pin_0, LED1.pin1
  N24: R1.Pin_1, Pi_Connector.IO13
  N25: U4.pin1, Pi_Connector.IO26
  N26: U4.pin3, Bell_CC.pin2
  N27: U4.pin4, Bell_CC.pin1
  N28: Pi_Connector.IO6, Sensor.pin2

notes:
  5V
  12V
  3.3V
  G-Pi Active
  CuriousJames.net\DIYACPCB
  v1.0
  ¯\_(ツ)_/¯
  R-Spare
  R-Srike On
  G-Bell 12V On

custom parts:
  AQT212GH: PhotoMOS GU 1 Form A High Capacity opto isolator. 4-pin high capacity of 1.1A, I/O isolation voltage of 5,000V
  l710a8ge dual led: KingBright L-710A8GE/11GD-RV T-1 (3mm) BI-LEVEL LED INDICATOR red/green.
  Logic Level Converter: 5V to/from 3.3V logic level converter
  TSR2 Series: Mini DC/DC Step-Down (Buck) Converter - 5V @ 1A output - TSR12450
  2.1mm DC Barrel Jack: 2.1mm DC Barrel Jack with Thru-Hole Connectors (breadboardable)
  Raspberry Pi Header 40pin: Raspberry Pi 40 pin header - for creating your own shields. (Mar 2020, bb: make breadboard friendly (.4in pin spacing) and add labels. Schematic add labels. PCB make oblong pins to allow routing traces between the pins.)
  Camdenboss CTB0158-8: Camdenboss CTB0158-8 5.08mm (0.2") Pitch Standard Profile 90 ̊ Rising Clamp Terminal, 8 pole The real-life connectors are modular, made up of two or three connector blocks slotted together. These can be further slotted together to make larger connectors. Fritzing part is derived from Screw terminals by Lionel Michel. Because of the offset between connection pins and screw terminals, these are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
  Camdenboss CTB0158-2: Camdenboss CTB0158-2 5.08mm (0.2") Pitch Standard Profile 90 ̊ Rising Clamp Terminal, 2 pole The real-life connectors are modular, made up of two or three connector blocks slotted together. These can be further slotted together to make larger connectors. Fritzing part is derived from Screw terminals by Lionel Michel. Because of the offset between connection pins and screw terminals, these are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
