# Fritzing sketch PCB Design (saved by Fritzing 0.9.4)
circuit board: 6.80001cm x 5.85cm
breadboards: 1

parts:
  LED2 = l710a8ge dual led [package=THT]
  LLC1 = Logic Level Converter [package="Breakout board"]
  U1-> = TSR2 Series
  R3 = Resistor [tolerance=±5% resistance=470 package=THT]
  PWR = LED - 5mm [color="Red (633nm)" package="5 mm [THT]"]
  R4 = Resistor [tolerance=±5% resistance=470 package=THT]
  R2 = Resistor [tolerance=±5% resistance=470 package=THT]
  R1 = Resistor [tolerance=±5% resistance=470 package=THT]
  LED1 = l710a8ge dual led [package=THT]
  R8 = Resistor [tolerance=±5% resistance=330 package=THT]
  R7 = Resistor [tolerance=±5% resistance=330 package=THT]
  Bell_CC = Camdenboss CTB0158-2 [package=THT]
  Strike = Camdenboss CTB0158-2 [package=THT]
  Sensor = Camdenboss CTB0158-2 [package=THT]
  3v3 = Camdenboss CTB0158-2 [package=THT]
  Bell_12V = Camdenboss CTB0158-2 [package=THT]
  R9 = Resistor [tolerance=±5% resistance=330 package=THT]
  R10 = Resistor [tolerance=±5% resistance=100k package=THT]
  C2 = Ceramic Capacitor [capacitance=0.1µF package="100 mil [THT, multilayer]"]
  R13 = Resistor [tolerance=±5% resistance=10k package=THT]
  R12 = Resistor [tolerance=±5% resistance=100k package=THT]
  C3 = Ceramic Capacitor [capacitance=0.1µF package="100 mil [THT, multilayer]"]
  Fuse4 = Fuse with Handler [part_number=Htc-15m]
  R11 = Resistor [tolerance=±5% resistance=10k package=THT]
  Door_Reader = Camdenboss CTB0158-8 [package=THT]
  U2 = AQT212GH [package="DIP (Dual Inline) [THT]"]
  U4 = AQT212GH [package="DIP (Dual Inline) [THT]"]
  U3 = AQT212GH [package="DIP (Dual Inline) [THT]"]
  Pi_Connector = Raspberry Pi Header - Pi Hat [package=THT]
  R5 = Resistor [tolerance=±5% resistance=100k package=THT]
  R6 = Resistor [tolerance=±5% resistance=10k package=THT]
  C1 = Ceramic Capacitor [capacitance=0.1µF package="100 mil [THT, multilayer]"]
  Exit_Button = Camdenboss CTB0158-2 [package=THT]
  12V__4A = 2.1mm DC Barrel Jack Generic

nets:
  N1: LED2.pin1, R3.Pin_0
  GND: LED2.pin2, LED2.pin4, LLC1.L-GND, LLC1.H-GND, U1->.GND, PWR.cathode, LED1.pin2, LED1.pin4, Strike.pin1, Sensor.pin1, 3v3.pin1, Bell_12V.pin1, C2.1, C3.1, Door_Reader.pin2, Door_Reader.pin8, U2.pin2, U4.pin2, U3.pin2, Pi_Connector.GND, C1.1, Exit_Button.pin1, 12V__4A.GND, 12V__4A.sleeve
  N2: LED2.pin3, R4.Pin_0
  N3: LLC1.LV1, Pi_Connector.IO5
  N4: LLC1.LV2, Pi_Connector.IO6
  N5: LLC1.LV, R8.Pin_1, R7.Pin_1, 3v3.pin2, R9.Pin_1, R10.Pin_0, R12.Pin_0, Pi_Connector.3V3, R5.Pin_0
  N6: LLC1.LV3, Pi_Connector.IO13
  N7: LLC1.LV4, Pi_Connector.IO19
  N8: LLC1.HV4, Door_Reader.pin3
  N9: LLC1.HV3, Door_Reader.pin4
  N10: LLC1.HV, U1->.OUT, Pi_Connector.5V
  N11: LLC1.HV2, Door_Reader.pin5
  N12: LLC1.HV1, Door_Reader.pin6
  N13: U1->.IN, Fuse4.Connector1
  N14: R3.Pin_1, Bell_12V.pin2, U4.pin4
  N15: PWR.anode, Fuse4.Connector2, Door_Reader.pin1, U4.pin3, U3.pin3, 12V__4A.center_(V+)
  N16: R4.Pin_1, Strike.pin2, U3.pin4
  N17: R2.Pin_0, LED1.pin3
  N18: R2.Pin_1, Pi_Connector.IO3
  N19: R1.Pin_0, LED1.pin1
  N20: R1.Pin_1, Pi_Connector.IO4
  N21: R8.Pin_0, U3.pin1, Pi_Connector.IO22#12
  N22: R7.Pin_0, U2.pin1, Pi_Connector.IO17
  N23: Bell_CC.pin1, U2.pin4
  N24: Bell_CC.pin2, U2.pin3
  N25: Sensor.pin2, R13.Pin_1, R12.Pin_1
  N26: R9.Pin_0, U4.pin1, Pi_Connector.IO22#14
  N27: R10.Pin_1, R11.Pin_1, Door_Reader.pin7
  N28: C2.0, R11.Pin_0, Pi_Connector.IO26
  N29: R13.Pin_0, C3.0, Pi_Connector.IO20
  N30: Pi_Connector.IO10, R6.Pin_0, C1.0
  N31: R5.Pin_1, R6.Pin_1, Exit_Button.pin2

notes:
  5V
  12V
  3.3V
  G-Pi Active
  CuriousJames.net\DIYACPCB
  v2.1
  ¯\_(ツ)_/¯
  R-UserDef
  R-Srike On
  G-Bell 12V On
  Don't forget that you're awesome

custom parts:
  l710a8ge dual led: KingBright L-710A8GE/11GD-RV T-1 (3mm) BI-LEVEL LED INDICATOR red/green.
  Logic Level Converter: 5V to/from 3.3V logic level converter
  TSR2 Series: Mini DC/DC Step-Down (Buck) Converter - 5V @ 1A output - TSR12450
  Camdenboss CTB0158-2: Camdenboss CTB0158-2 5.08mm (0.2") Pitch Standard Profile 90 ̊ Rising Clamp Terminal, 2 pole The real-life connectors are modular, made up of two or three connector blocks slotted together. These can be further slotted together to make larger connectors. Fritzing part is derived from Screw terminals by Lionel Michel. Because of the offset between connection pins and screw terminals, these are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
  Camdenboss CTB0158-8: Camdenboss CTB0158-8 5.08mm (0.2") Pitch Standard Profile 90 ̊ Rising Clamp Terminal, 8 pole The real-life connectors are modular, made up of two or three connector blocks slotted together. These can be further slotted together to make larger connectors. Fritzing part is derived from Screw terminals by Lionel Michel. Because of the offset between connection pins and screw terminals, these are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
  AQT212GH: PhotoMOS GU 1 Form A High Capacity opto isolator. 4-pin high capacity of 1.1A, I/O isolation voltage of 5,000V
  Raspberry Pi Header - Pi Hat: Raspberry Pi 40 pin header - for creating your own shields. (Mar 2020, bb: make breadboard friendly (.4in pin spacing) and add labels. Schematic add labels. PCB make oblong pins to allow routing traces between the pins.)
  2.1mm DC Barrel Jack Generic: 2.1mm DC Barrel Jack with Thru-Hole Connectors (breadboardable)
